// Logisim project MMU-skeleton.circ as structural Verilog: 2 circuits, main circuit main
module main (
  input  [15:0] Logical_Address,
  input  V,
  input  W,
  input  R,
  input  [7:0] frame_num,
  input  Privilege,
  input  RAM_USE,
  input  READ,
  input  WRITE,
  output [15:0] PHYSICAL_ADDRESS,
  output [7:0] Page_num,
  output RAM_USE_2,
  output READ_2,
  output WRITE_2,
  output EXCEPTION
);

  wire [7:0] Actual_Pagetable_dout;
  wire [10:8] Actual_Pagetable_dout_2;

  RAM #(.dataWidth(11)) Actual_Pagetable (
    .addr(Logical_Address[15:8]), .dout({Actual_Pagetable_dout_2, Actual_Pagetable_dout}));  // open: we, clk, din
  MMU mmu_1 (
    .Exception(EXCEPTION), .Ram_Use__out(RAM_USE_2), .Write__out(WRITE_2), .Read__out(READ_2),
    .Privilege(Privilege), .Ram_Use__in(RAM_USE), .Read__in(READ), .Write__in(WRITE), .Valid(V),
    .Unpriv_Write(W), .Unpriv_Read(R));

  assign Page_num = Logical_Address[15:8];
  assign PHYSICAL_ADDRESS = {frame_num, Logical_Address[7:0]};

  // Notes on the sheet:
  //   (page table entry)
  //   (for testing/demo)
endmodule

module MMU (
  input  Valid,
  input  Unpriv_Write,
  input  Unpriv_Read,
  input  Privilege,
  input  Ram_Use__in,
  input  Read__in,
  input  Write__in,
  output Ram_Use__out,
  output Write__out,
  output Read__out,
  output Exception
);

  wire and_1_out, and_2_out, and_3_out, and_4_out, and_5_out, and_6_out, and_7_out, and_8_out, and_9_out,
       not_1_out, or_1_out, or_3_out;

  not not_1 (not_1_out, Privilege);
  and and_1 (and_1_out, ~Unpriv_Write, Write__in, Privilege);  // AND_Gate
  and and_2 (and_2_out, Unpriv_Write, Write__in);
  and and_3 (and_3_out, not_1_out, Write__in);
  or or_1 (or_1_out, and_3_out, and_2_out);
  and and_4 (and_4_out, ~Unpriv_Read, Read__in, Privilege);  // AND_Gate
  and and_5 (and_5_out, Unpriv_Read, Read__in);
  and and_6 (and_6_out, not_1_out, Read__in);
  or or_2 (Exception, and_4_out, ~Valid, and_1_out);  // OR_Gate
  or or_3 (or_3_out, and_6_out, and_5_out);
  and and_7 (and_7_out, Ram_Use__in, ~Exception);  // AND_Gate
  and and_8 (and_8_out, Ram_Use__in, Write__in, ~Exception, ~Read__in);  // AND_Gate
  and and_9 (and_9_out, Ram_Use__in, Read__in, ~Exception, ~Write__in);  // AND_Gate
  Multiplexer #(.enable("false")) multiplexer_1 (.in0(1'b0), .in1(Ram_Use__in), .out(Ram_Use__out), .sel(and_7_out));
  Multiplexer #(.enable("false")) multiplexer_2 (.in0(1'b0), .in1(or_1_out), .out(Write__out), .sel(and_8_out));
  Multiplexer #(.enable("false")) multiplexer_3 (.in0(1'b0), .in1(or_3_out), .out(Read__out), .sel(and_9_out));

  // Notes on the sheet:
  //   Question 2
  //   Design thinking:
  //   1. Send Ram Use, Read, and Write inputs to multiplexers to their respective outputs.
  //   2. The inputs will be selected for outputs only if (for Ram Use) Ram Use itself is enabled and there is no exception,
  //   if (for Write) Ram Use and Write are enabled and there is no exception or read and write happening simultaneously, and
  //   if (for Read) Ram Use and Read are enabled and there is no exception or read and write happening simultaneously.
  //   3. Exception checking is done by seeing if privilege is set to user mode (1) but either the unpriv write or read (depending
  //   on which is indicated as an input) is disabled or if invalid. Exception is also enabled if the page is invalid.
  //   4. For checking if running in privileged mode (in which case, the enabled read or write will simply go through) or if running in
  //   user mode (in which case, the unpriv bit must also be enabled for the enabled read or write to go through).
  //   5. When read and write are enabled simultaneously, the data will not be outputted to either write or read.
  //   Testing:
  //   Privilege | Ram Use (in) | Read (in) | Write (in) | Valid | Unpriv Write | Unpriv Read | Ram Use (out) | Write (out) | Read (out) | Exception
  //   0 | 1 | 1 | 0 | 1 | 0 | 0 | 1 | 0 | 1 | 0
  //   0 | 1 | 1 | 0 | 0 | 0 | 0 | 0 | 0 | 0 | 1
  //   1 | 1 | 0 | 1 | 1 | 1 | 0 | 1 | 1 | 0 | 0
  //   1 | 1 | 0 | 1 | 1 | 0 | 0 | 0 | 0 | 0 | 1
  //   0 | 1 | 1 | 1 | 1 | 0 | 0 | 1 | 0 | 0 | 0
  //   0 | 0 | 1 | 0 | 1 | 0 | 0 | 0 | 0 | 0 | 0
endmodule
