// Logisim project uarch-skeleton-2021.circ as structural Verilog: 16 circuits, main circuit regwriter
module dpath (
  input  Reset,
  input  in_2,
  output out_3
);

  wire aluBsel, aluOPsel, and_1_out, and_2_out, and_3_out, and_4_out, and_5_out, and_6_out, and_7_out,
       and_8_out, and_9_out, and_11_out, and_12_out, cnd_1_cnd, comparator_1_eq, comparator_2_eq,
       comparator_2_lt, comparator_3_eq, comparator_5_lt, comparator_6_gt, D_RAMread, D_RAMuse, D_RAMWrite,
       DMemReady, DMemReq, DMemWrite, dstEsel, dstMreq, enPRIVmode, enUSERmode, exception, I_RAMread,
       I_RAMuse, IMemReady, IMemReq, io_1_tty_clear, io_1_tty_enable, isException, kbyte_buddy_1_sel,
       kbyte_buddy_2_sel, ldCC, ldMAR, ldMDR, ldPC, MARsel, MDRsel, multiplexer_11_out, or_1_out, or_3_out,
       or_4_out, or_6_out, or_7_out, or_9_out, or_10_out, or_12_out, privCODEfail, privmode, regreader_1_clr,
       regreader_1_clr_2, regreader_1_clr_3, regreader_1_clr_4, regreader_1_clr_5, regreader_1_clr_6,
       regreader_1_clr_7, regreader_1_clr_8, regwriter_1_en, regwriter_1_en_2, regwriter_1_en_3,
       regwriter_1_en_4, regwriter_1_en_5, regwriter_1_en_6, regwriter_1_en_7, regwriter_1_en_8, srcAsel,
       srcBsel, undriven, valCsel, valInstruct, xor_1_out, xor_2_out;
  wire [1:0] aluAsel, dstEreq, multiplexer_2_out, multiplexer_3_out, multiplexer_15_out, multiplexer_16_out,
       multiplexer_20_out, multiplexer_21_out, multiplexer_23_out, multiplexer_24_out, multiplexer_25_out,
       multiplexer_26_out, multiplexer_27_out, multiplexer_28_out, newPCsel, or_2_out, or_5_out, or_8_out,
       or_11_out, or_13_out, or_14_out, PCIncSel;
  wire [2:0] alu_1_cc, bit_extender_1_out, bit_extender_2_out, bit_extender_3_out, bit_extender_4_out, cc;
  wire [3:0] icode, ifun, isplit_1_ra, isplit_1_rb, multiplexer_8_out, multiplexer_9_out, multiplexer_10_out,
       multiplexer_14_out;
  wire [5:0] Current_State_q, microsequencer_1_nextstate;
  wire [6:0] io_1_out_13;
  wire [7:0] code_data, D_Data_from_RAM, D_Data_to_RAM, data_dout, FSM_ROM0_data, I_Data_from_RAM,
       io_1_outgoing_data, ishim_1_out_6, ishim_1_out_7, ishim_1_out_8, ishim_1_out_9, ishim_1_out_10,
       ishim_1_out_11;
  wire [9:0] controlled_buffer_1_out, controlled_buffer_2_out, kbyte_buddy_1_ram_addr, kbyte_buddy_2_ram_addr;
  wire [11:0] FSM_ROM1_data;
  wire [31:0] adder_1_out, alu_1_vale, currPC, D_RAMAddr, dhsim_1_dataout, eax_q, ebp_q, ebx_q, ecx_q, edi_q,
       edx_q, esi_q, esp_q, I_RAMAddr, isplit_1_d_v, isplit_1_dest, MAR_q, MDR_q, multiplexer_1_out,
       multiplexer_4_out, multiplexer_6_out, multiplexer_7_out, multiplexer_12_out, multiplexer_13_out,
       multiplexer_17_out, multiplexer_18_out, multiplexer_19_out, multiplexer_22_out, newPC, possiblePC,
       regreader_1_vala, regreader_1_valb, regwriter_1_d0, regwriter_1_d1, regwriter_1_d2, regwriter_1_d3,
       regwriter_1_d4, regwriter_1_d5, regwriter_1_d6, regwriter_1_d7;

  Register #(.width(32)) PC (.D(newPC), .en(ldPC), .Q(currPC), .clk(out_3), .clr(Reset));
  Clock Clock (.out(out_3));
  or or_1 (or_1_out, D_RAMWrite, D_RAMread);
  // Probe on I_RAMuse
  // Probe on I_RAMAddr
  // Probe on IMemReq
  // Probe on PCIncSel
  ROM #(.addrWidth(6), .dataWidth(32)) FSM_ROM0 (
    .addr(Current_State_q),
    .data({IMemReq, PCIncSel, valCsel, srcAsel, srcBsel, dstEsel, dstEreq, dstMreq, aluAsel, aluBsel, aluOPsel, ldCC, MARsel, ldMAR, MDRsel, ldMDR, DMemReq, DMemWrite, newPCsel, ldPC, FSM_ROM0_data}));
  Register #(.width(6)) Current_State (
    .D(microsequencer_1_nextstate), .Q(Current_State_q), .clk(out_3), .clr(Reset));  // open: en
  ROM #(.addrWidth(6), .dataWidth(12)) FSM_ROM1 (.addr(Current_State_q), .data(FSM_ROM1_data));
  and and_1 (and_1_out, D_RAMuse, or_1_out);
  and and_2 (and_2_out, I_RAMuse, I_RAMread);
  xor xor_1 (xor_1_out, D_RAMuse, I_RAMuse);
  xor xor_2 (xor_2_out, D_RAMread, I_RAMread);
  Demultiplexer #(.enable("false"), .select(2), .width(8)) demultiplexer_1 (
    .out1(D_Data_from_RAM), .out2(I_Data_from_RAM), .in(io_1_outgoing_data), .sel(or_2_out));  // open: out0, out3
  // Probe on multiplexer_1_out
  Multiplexer #(.enable("false"), .select(2), .width(32)) multiplexer_1 (
    .in0(32'h1), .in1(32'h2), .in2(32'h5), .in3(32'h6), .out(multiplexer_1_out), .sel(PCIncSel));
  // Probe on I_RAMread
  // Probe on valCsel
  Multiplexer #(.enable("false"), .width(2)) multiplexer_2 (
    .in0(2'b00), .in1(2'b01), .out(multiplexer_2_out), .sel(and_1_out));
  Multiplexer #(.enable("false"), .width(2)) multiplexer_3 (
    .in0(2'b00), .in1(2'b10), .out(multiplexer_3_out), .sel(and_2_out));
  Adder #(.width(32)) adder_1 (.a(multiplexer_1_out), .b(currPC), .out(adder_1_out), .cin(1'b0));  // open: cout
  CND cnd_1 (.CND(cnd_1_cnd), .ZSO(cc), .ifun(ifun));
  // Probe on IMemReady
  // Probe on I_Data_from_RAM
  // Probe on srcAsel
  // Probe on or_2_out
  assign or_2_out = multiplexer_2_out | multiplexer_3_out;  // OR_Gate or_2, 2 bits wide
  Multiplexer #(.enable("false"), .select(2), .width(32)) multiplexer_4 (
    .in1(D_RAMAddr), .in2(I_RAMAddr), .out(multiplexer_4_out), .sel(or_2_out));  // open: in0, in3
  and and_3 (and_3_out, ~privmode, xor_1_out);  // AND_Gate
  Multiplexer #(.enable("false"), .select(2), .width(32)) multiplexer_5 (
    .in0(adder_1_out), .in1(multiplexer_7_out), .in2(dhsim_1_dataout), .in3(multiplexer_6_out),
    .out(possiblePC), .sel(newPCsel));
  Multiplexer #(.enable("false"), .width(32)) multiplexer_6 (
    .in0(adder_1_out), .in1(multiplexer_7_out), .out(multiplexer_6_out), .sel(cnd_1_cnd));
  isplit isplit_1 (
    .Dest(isplit_1_dest), .D_V(isplit_1_d_v), .rA(isplit_1_ra), .rB(isplit_1_rb), .icode(icode), .ifun(ifun),
    .B1(ishim_1_out_7), .B2(ishim_1_out_8), .B3(ishim_1_out_9), .B4(ishim_1_out_10), .B5(ishim_1_out_11),
    .B0(ishim_1_out_6));
  ishim ishim_1 (
    .out_7(ishim_1_out_7), .out_8(ishim_1_out_8), .out_9(ishim_1_out_9), .out_10(ishim_1_out_10),
    .out_11(ishim_1_out_11), .out_6(ishim_1_out_6), .done(IMemReady), .RAMuse(I_RAMuse), .out_14(I_RAMAddr),
    .RAMread(I_RAMread), .in_2(currPC), .reset(Reset), .req(IMemReq), .clock(out_3), .in_5(I_Data_from_RAM));
  // Probe on srcBsel
  // Probe on dstEsel
  // Probe on multiplexer_4_out
  // Probe on io_1_outgoing_data
  // Probe on icode
  // Probe on ifun
  Multiplexer #(.enable("false"), .width(32)) multiplexer_7 (
    .in0(isplit_1_dest), .in1(isplit_1_d_v), .out(multiplexer_7_out), .sel(valCsel));
  // Probe on multiplexer_7_out
  // Probe on dstEreq
  // Probe on FSM_ROM1_data[9:4]
  // Probe on D_Data_to_RAM
  io io_1 (
    .Outgoing_Data(io_1_outgoing_data), .out_13(io_1_out_13), .TTY_Enable(io_1_tty_enable),
    .TTY_Clear(io_1_tty_clear), .TTY_Ready(in_2), .RAM_Use(and_3_out), .in_4(multiplexer_4_out),
    .in_5(D_Data_to_RAM), .RAM_Read(xor_2_out), .RAM_Write(D_RAMWrite), .reset(Reset));  // open: KB_read_enable, KB_Clear, in_2, KB_Status
  // Probe on isplit_1_ra
  // Probe on isplit_1_rb
  // Probe on dstMreq
  Multiplexer #(.enable("false"), .width(4)) multiplexer_8 (
    .in0(isplit_1_rb), .in1(4'b0100), .out(multiplexer_8_out), .sel(dstEsel));
  Multiplexer #(.enable("false"), .width(4)) multiplexer_9 (
    .in0(isplit_1_ra), .in1(4'b0100), .out(multiplexer_9_out), .sel(srcAsel));
  Multiplexer #(.enable("false"), .width(4)) multiplexer_10 (
    .in0(isplit_1_rb), .in1(4'b0100), .out(multiplexer_10_out), .sel(srcBsel));
  // Probe on aluAsel
  Bit_Extender #(.in_width(4), .out_width(3), .\type ("zero")) bit_extender_1 (
    .in(multiplexer_8_out), .out(bit_extender_1_out));
  Multiplexer #(.enable("false"), .select(2)) multiplexer_11 (
    .in0(1'b0), .in1(1'b1), .in2(cnd_1_cnd), .out(multiplexer_11_out), .sel(dstEreq));  // open: in3
  Bit_Extender #(.in_width(4), .out_width(3), .\type ("zero")) bit_extender_2 (
    .in(isplit_1_ra), .out(bit_extender_2_out));
  Bit_Extender #(.in_width(4), .out_width(3), .\type ("zero")) bit_extender_3 (
    .in(multiplexer_9_out), .out(bit_extender_3_out));
  Bit_Extender #(.in_width(4), .out_width(3), .\type ("zero")) bit_extender_4 (
    .in(multiplexer_10_out), .out(bit_extender_4_out));
  Comparator #(.width(4)) comparator_1 (.a(multiplexer_10_out), .b(4'b1111), .eq(comparator_1_eq));  // open: gt, lt
  // Probe on aluBsel
  Microsequencer microsequencer_1 (
    .NextState(microsequencer_1_nextstate), .CurrentState(Current_State_q), .select(FSM_ROM1_data[11:10]),
    .icode(icode), .valN(FSM_ROM1_data[9:4]), .DMemReady(DMemReady), .IMemReady(IMemReady),
    .exception(exception), .privCODEfail(privCODEfail));
  // Probe on microsequencer_1_nextstate
  TTY tty_1 (.data(io_1_out_13), .clk(out_3), .we(io_1_tty_enable), .clr(io_1_tty_clear));
  // Probe on io_1_out_13
  Register #(.width(32)) eax (.D(regwriter_1_d0), .en(regwriter_1_en), .Q(eax_q), .clk(out_3), .clr(regreader_1_clr));
  regwriter regwriter_1 (
    .D5(regwriter_1_d5), .EN_6(regwriter_1_en_6), .D6(regwriter_1_d6), .EN_7(regwriter_1_en_7),
    .D7(regwriter_1_d7), .EN_8(regwriter_1_en_8), .D0(regwriter_1_d0), .EN(regwriter_1_en),
    .D1(regwriter_1_d1), .EN_2(regwriter_1_en_2), .D2(regwriter_1_d2), .EN_3(regwriter_1_en_3),
    .D3(regwriter_1_d3), .EN_4(regwriter_1_en_4), .D4(regwriter_1_d4), .EN_5(regwriter_1_en_5),
    .reqE(multiplexer_11_out), .valE(alu_1_vale), .dstE(bit_extender_1_out), .reqM(dstMreq),
    .valM(dhsim_1_dataout), .dstM(bit_extender_2_out));
  Register #(.width(32)) ecx (
    .D(regwriter_1_d1), .en(regwriter_1_en_2), .Q(ecx_q), .clk(out_3), .clr(regreader_1_clr_2));
  Register #(.width(32)) edx (
    .D(regwriter_1_d2), .en(regwriter_1_en_3), .Q(edx_q), .clk(out_3), .clr(regreader_1_clr_3));
  Register #(.width(32)) ebx (
    .D(regwriter_1_d3), .en(regwriter_1_en_4), .Q(ebx_q), .clk(out_3), .clr(regreader_1_clr_4));
  Register #(.width(32)) esp (
    .D(regwriter_1_d4), .en(regwriter_1_en_5), .Q(esp_q), .clk(out_3), .clr(regreader_1_clr_5));
  Register #(.width(32)) ebp (
    .D(regwriter_1_d5), .en(regwriter_1_en_6), .Q(ebp_q), .clk(out_3), .clr(regreader_1_clr_6));
  Register #(.width(32)) esi (
    .D(regwriter_1_d6), .en(regwriter_1_en_7), .Q(esi_q), .clk(out_3), .clr(regreader_1_clr_7));
  Register #(.width(32)) edi (
    .D(regwriter_1_d7), .en(regwriter_1_en_8), .Q(edi_q), .clk(out_3), .clr(regreader_1_clr_8));
  // Probe on aluOPsel
  regreader regreader_1 (
    .valA(regreader_1_vala), .valB(regreader_1_valb), .CLR(regreader_1_clr), .CLR_2(regreader_1_clr_2),
    .CLR_3(regreader_1_clr_3), .CLR_4(regreader_1_clr_4), .CLR_5(regreader_1_clr_5),
    .CLR_6(regreader_1_clr_6), .CLR_7(regreader_1_clr_7), .CLR_8(regreader_1_clr_8), .reset(Reset),
    .srcA(bit_extender_3_out), .srcB(bit_extender_4_out), .Q_8(edi_q), .Q(eax_q), .Q_2(ecx_q), .Q_3(edx_q),
    .Q_4(ebx_q), .Q_5(esp_q), .Q_6(ebp_q), .Q_7(esi_q));
  // Probe on ldCC
  or or_3 (or_3_out, D_RAMWrite, D_RAMread);
  // Probe on regreader_1_vala
  // Probe on regreader_1_valb
  // Probe on multiplexer_7_out
  // Probe on ldMAR
  // Probe on MARsel
  and and_4 (and_4_out, D_RAMuse, or_3_out);
  and and_5 (and_5_out, I_RAMuse, I_RAMread);
  Multiplexer #(.enable("false"), .select(2), .width(32)) multiplexer_12 (
    .in0(regreader_1_vala), .in1(multiplexer_7_out), .in2(32'h4), .in3(32'hfffffffc),
    .out(multiplexer_12_out), .sel(aluAsel));
  Multiplexer #(.enable("false"), .width(32)) multiplexer_13 (
    .in0(regreader_1_valb), .in1({32{1'b0}}), .out(multiplexer_13_out), .sel(or_4_out));
  or or_4 (or_4_out, comparator_1_eq, aluBsel);
  Multiplexer #(.enable("false"), .width(4)) multiplexer_14 (
    .in0(4'b0000), .in1(ifun), .out(multiplexer_14_out), .sel(aluOPsel));
  // Probe on MDRsel
  Multiplexer #(.enable("false"), .width(2)) multiplexer_15 (
    .in0(2'b00), .in1(2'b01), .out(multiplexer_15_out), .sel(and_4_out));
  Multiplexer #(.enable("false"), .width(2)) multiplexer_16 (
    .in0(2'b00), .in1(2'b10), .out(multiplexer_16_out), .sel(and_5_out));
  alu alu_1 (
    .valE(alu_1_vale), .CC(alu_1_cc), .aluB(multiplexer_13_out), .aluA(multiplexer_12_out),
    .aluOP(multiplexer_14_out));
  // Probe on ldMDR
  // Probe on DMemReq
  // Probe on or_5_out
  assign or_5_out = multiplexer_15_out | multiplexer_16_out;  // OR_Gate or_5, 2 bits wide
  Multiplexer #(.enable("false"), .select(2), .width(32)) multiplexer_17 (
    .in1(D_RAMAddr), .in2(I_RAMAddr), .out(multiplexer_17_out), .sel(or_5_out));  // open: in0, in3
  // Probe on I_RAMAddr
  // Probe on cc
  Register #(.width(3)) u_CC (.D(alu_1_cc), .en(ldCC), .Q(cc), .clk(out_3), .clr(Reset));
  // Probe on DMemWrite
  kbyte_buddy kbyte_buddy_1 (
    .ram_addr(kbyte_buddy_1_ram_addr), .sel(kbyte_buddy_1_sel), .addr(multiplexer_17_out),
    .addr_prefix({32{1'b0}}), .\use (or_6_out));
  or or_6 (or_6_out, and_4_out, and_5_out);
  or or_7 (or_7_out, D_RAMWrite, D_RAMread);
  and and_6 (and_6_out, D_RAMuse, or_7_out);
  and and_7 (and_7_out, I_RAMuse, I_RAMread);
  // Probe on adder_1_out
  // Probe on alu_1_vale
  Multiplexer #(.enable("false"), .width(32)) multiplexer_18 (
    .in0(regreader_1_vala), .in1(adder_1_out), .out(multiplexer_18_out), .sel(MDRsel));
  Multiplexer #(.enable("false"), .width(32)) multiplexer_19 (
    .in0(alu_1_vale), .in1(regreader_1_vala), .out(multiplexer_19_out), .sel(MARsel));
  // Probe on newPCsel
  ROM #(.addrWidth(10)) code (.addr(controlled_buffer_1_out), .data(code_data));
  assign controlled_buffer_1_out = kbyte_buddy_1_sel ? kbyte_buddy_1_ram_addr : 10'bz;  // Controlled_Buffer controlled_buffer_1
  // Probe on multiplexer_17_out
  Multiplexer #(.enable("false"), .width(2)) multiplexer_20 (
    .in0(2'b00), .in1(2'b01), .out(multiplexer_20_out), .sel(and_6_out));
  Multiplexer #(.enable("false"), .width(2)) multiplexer_21 (
    .in0(2'b00), .in1(2'b10), .out(multiplexer_21_out), .sel(and_7_out));
  Register #(.width(32)) MDR (.D(multiplexer_18_out), .en(ldMDR), .Q(MDR_q), .clk(out_3), .clr(Reset));
  Register #(.width(32)) MAR (.D(multiplexer_19_out), .en(ldMAR), .Q(MAR_q), .clk(out_3), .clr(Reset));
  // Probe on ldPC
  // Probe on or_8_out
  assign or_8_out = multiplexer_20_out | multiplexer_21_out;  // OR_Gate or_8, 2 bits wide
  Multiplexer #(.enable("false"), .select(2), .width(32)) multiplexer_22 (
    .in1(D_RAMAddr), .in2(I_RAMAddr), .out(multiplexer_22_out), .sel(or_8_out));  // open: in0, in3
  // Probe on D_RAMuse
  // Probe on D_RAMAddr
  and and_8 (and_8_out, D_RAMuse, D_RAMread);
  and and_9 (and_9_out, I_RAMuse, I_RAMread);
  kbyte_buddy kbyte_buddy_2 (
    .ram_addr(kbyte_buddy_2_ram_addr), .sel(kbyte_buddy_2_sel), .addr(multiplexer_22_out),
    .addr_prefix(32'hffff0000), .\use (or_9_out));
  or or_9 (or_9_out, and_6_out, and_7_out);
  // Probe on dhsim_1_dataout
  // Probe on D_RAMread
  // Probe on D_RAMWrite
  // Probe on D_Data_to_RAM
  D_Flip_Flop d_ff_1 (.Q(privmode), .preset(enUSERmode), .reset(or_10_out));  // open: clk, D, Qn
  or or_10 (or_10_out, exception, Reset, enPRIVmode);
  // Probe on {icode, ifun}
  ROM #(.dataWidth(1)) validInstructionsRom (.addr({icode, ifun}));  // open: data
  Multiplexer #(.enable("false"), .width(2)) multiplexer_23 (
    .in0(2'b00), .in1(2'b01), .out(multiplexer_23_out), .sel(and_8_out));
  assign or_11_out = multiplexer_23_out | multiplexer_24_out;  // OR_Gate or_11, 2 bits wide
  Multiplexer #(.enable("false"), .width(2)) multiplexer_24 (
    .in0(2'b00), .in1(2'b10), .out(multiplexer_24_out), .sel(and_9_out));
  // Probe on code_data
  assign controlled_buffer_2_out = kbyte_buddy_2_sel ? kbyte_buddy_2_ram_addr : 10'bz;  // Controlled_Buffer controlled_buffer_2
  // Probe on multiplexer_22_out
  dhsim dhsim_1 (
    .out_9(D_Data_to_RAM), .RAMwrite(D_RAMWrite), .RAMread(D_RAMread), .done(DMemReady),
    .DataOut(dhsim_1_dataout), .RAMuse(D_RAMuse), .out_14(D_RAMAddr), .in_2(D_Data_from_RAM), .in_1(MAR_q),
    .DMem_Write(DMemWrite), .req(DMemReq), .reset(Reset), .clock(out_3), .in_3(MDR_q));
  // Probe on D_Data_from_RAM
  // Probe on or_11_out
  Demultiplexer #(.enable("false"), .select(2), .width(8)) demultiplexer_2 (
    .out1(D_Data_from_RAM), .out2(I_Data_from_RAM), .in(code_data), .sel(or_11_out));  // open: out0, out3
  // Probe on controlled_buffer_2_out
  RAM #(.addrWidth(10)) data (
    .addr(controlled_buffer_2_out), .we(D_RAMWrite), .clk(out_3), .din(D_Data_to_RAM), .dout(data_dout));
  // Probe on dhsim_1_dataout
  // Probe on DMemReady
  // Probe on ifun
  Comparator #(.mode("unsigned"), .width(4)) comparator_2 (
    .a(ifun), .b(4'b0001), .eq(comparator_2_eq), .lt(comparator_2_lt));  // open: gt
  // Probe on icode
  Comparator #(.mode("unsigned"), .width(4)) comparator_3 (
    .a(icode), .b(4'b1101), .eq(comparator_3_eq));  // open: gt, lt
  and and_10 (privCODEfail, ~undriven, ~isException, ~privmode);  // AND_Gate
  Comparator #(.mode("unsigned")) comparator_4 (.a({icode, ifun}), .b(8'he0), .eq(isException));  // open: gt, lt
  Multiplexer #(.enable("false"), .width(2)) multiplexer_25 (
    .in0(2'b00), .in1(2'b01), .out(multiplexer_25_out), .sel(and_11_out));
  Multiplexer #(.enable("false"), .width(2)) multiplexer_26 (
    .in0(2'b00), .in1(2'b10), .out(multiplexer_26_out), .sel(and_12_out));
  and and_11 (and_11_out, D_RAMuse, D_RAMread);
  and and_12 (and_12_out, I_RAMuse, I_RAMread);
  and and_13 (enUSERmode, comparator_2_lt, comparator_3_eq);
  and and_14 (enPRIVmode, comparator_2_eq, comparator_3_eq);
  and and_15 (exception, ~valInstruct, ~privCODEfail, or_12_out);  // AND_Gate
  or or_12 (or_12_out, comparator_5_lt, comparator_6_gt);
  Comparator #(.mode("unsigned"), .width(32)) comparator_5 (
    .a(currPC), .b(32'h1ff), .lt(comparator_5_lt));  // open: gt, eq
  Comparator #(.mode("unsigned"), .width(32)) comparator_6 (
    .a(currPC), .b(32'h299), .gt(comparator_6_gt));  // open: eq, lt
  and and_16 (valInstruct, undriven, ~isException);  // AND_Gate
  // Probe on or_13_out
  assign or_13_out = multiplexer_25_out | multiplexer_26_out;  // OR_Gate or_13, 2 bits wide
  // Probe on data_dout
  Demultiplexer #(.enable("false"), .select(2), .width(8)) demultiplexer_3 (
    .out1(D_Data_from_RAM), .out2(I_Data_from_RAM), .in(data_dout), .sel(or_13_out));  // open: out0, out3
  Multiplexer #(.enable("false"), .width(2)) multiplexer_27 (
    .in0(2'b00), .in1(2'b01), .out(multiplexer_27_out), .sel(enPRIVmode));
  assign or_14_out = multiplexer_27_out | multiplexer_28_out;  // OR_Gate or_14, 2 bits wide
  Multiplexer #(.enable("false"), .width(2)) multiplexer_28 (
    .in0(2'b00), .in1(2'b10), .out(multiplexer_28_out), .sel(exception));
  // Probe on or_14_out
  Multiplexer #(.enable("false"), .select(2), .width(32)) multiplexer_29 (
    .in0(possiblePC), .in1(32'h100), .in2(32'h1ff), .out(newPC), .sel(or_14_out));  // open: in3
  // Probe on newPC

  // Other names for the same wires on the sheet: Clock = out_3

  // Notes on the sheet:
  //   Y86 Skeleton
  //   Feb 11, 2021
  //   connect to memory!
  //   Fetch
  //   contents of FSM_ROM0 (hex, n*v repeats v):
  //   80000000 0 1800 0 1000 0 400000 1000 0 500 39*0 100 21080100 70980100 7010a100 70108100 20860100
  //   40000700 46b0e300 ea18000 26b0a100 2ea18100 70960100 6b0e100 6b0e100
  //   contents of FSM_ROM1 (hex, n*v repeats v):
  //   410 c00 430 800 450 860 400 480 890 400 39*0 400 400 400 420 440 400 400 420 470 420 440 400 420 420
  //   valP
  //   valM
  //   IR[1:4]
  //   IR[2:5]
  //   Decode/Write-Back
  //   SWS and Taylor Cathcart and Vijay Kothari, based on a skeleton from Matt Kretchmar
  //   rB == F?
  //   Execute
  //   0 add
  //   Memory
  //   PC
  //   contents of code (hex, n*v repeats v):
  //   30 f4 0 1 ff ff 30 f2 c 2 0 0 80 d 1 0 0 d0 70 0 3 235*0 30 f2 11 2 0 0 80 d 1 0 0 d0 90 30 f6 4*0
  //   30 f7 1 0 0 0 30 f3 ff 0 0 0 50 2 4*0 62 30 73 38 1 0 0 80 39 1 0 0 60 72 70 1f 1 0 0 90 50 1f 8 fe
  //   ff 0 60 61 73 39 1 0 0 40 f c fe ff 0 90 179*0 30 f2 17 2 0 0 80 d 1 0 0 0 48 69 21 20 0 59 65 73 3f
  //   20 0 55 68 2d 6f 68 21 20 226*0 d1 10 10 e0 10
  //   connect to memory (and io,
  //    pretending to be memory)
  //   contents of validInstructionsRom (hex, n*v repeats v):
  //   1 15*0 1 15*0 7*1 9*0 1 15*0 1 15*0 1 15*0 4*1 12*0 7*1 9*0 1 15*0 1 15*0 1 15*0 1 15*0 4*1 12*0 1 1
  //   14*0 1
  //   A halt is issued when the instruction is bad,
  //   the instruction is not the exception handling
  //   instruction, and the instruction is being run
  //   in privileged mode. When these conditions
  //   hold, privCODEfail is enabled, which is fed
  //   to the microsequencer where we send halt
  //   as the next state.
  //   An exception is thrown when the instruction is bad,
  //   the bad instruction did not fail due to being run in
  //   privileged mode, and we are not currently in the
  //   exception handling address space. Exception is fed
  //   to the microsequencer, where, if enabled, the exception
  //   handling state is sent as the next state.
  //   explanation of new tunnels:
  //   - privmode indicates whether we are running in
  //      privileged mode (0) or user mode (1).
  //   - enUSERmode, when enabled, sets the privmode
  //      to 1 (user mode).
  //   - enPRIVmode, when enabled, sets the privmode
  //      to 0 (privileged mode).
  //   - exception is enabled when we try running a bad
  //      instruction in user mode. (leads to exception handler)
  //   - privCODEfail is enabled when we try running a
  //      bad instruction in privileged mode. (leads to halt)
  //   - valInstruct is enabled when we use a ROM containing
  //      all valid (not bad) instructions to check if the instruction
  //      exists.
  //   - isException indicates whether or not we are looking at
  //      the instructions for the exception handling instruction.
  //   - currPC is the current value in the program counter.
  //   - possiblePC is the value that results from incrementing it
  //      as necessary as instructions are run.
  //   - newPC is the value that results from checking whether or
  //      not we entered privileged mode or if an exception was
  //      thrown.
  //   If we have entered privileged mode (as a
  //   result of sysenter), then we set the next PC
  //   to be 0x100.
  //   If we have an exception thrown, then we set
  //   the next PC to be 0x1ff, which becomes 0x200
  //   after the PC is incremented, which takes us to the
  //   exception handling code.
  //   enUSERmode is enabled when the
  //   instruction is d0.
  //   enPRIVmode is enabled when the
  //   instruction is d1.
endmodule

module isplit (
  input  [7:0] B0,
  input  [7:0] B1,
  input  [7:0] B2,
  input  [7:0] B3,
  input  [7:0] B4,
  input  [7:0] B5,
  output [3:0] icode,
  output [3:0] ifun,
  output [3:0] rA,
  output [3:0] rB,
  output [31:0] Dest,
  output [31:0] D_V
);


  assign D_V = {B5, B4, B3, B2};
  assign Dest = {B4, B3, B2, B1};
  assign icode = B0[7:4];
  assign ifun = B0[3:0];
  assign rA = B1[7:4];
  assign rB = B1[3:0];
endmodule

module regreader (
  input  reset,
  input  [2:0] srcA,
  input  [31:0] Q,
  input  [2:0] srcB,
  input  [31:0] Q_2,
  input  [31:0] Q_3,
  input  [31:0] Q_4,
  input  [31:0] Q_5,
  input  [31:0] Q_6,
  input  [31:0] Q_7,
  input  [31:0] Q_8,
  output [31:0] valA,
  output CLR,
  output [31:0] valB,
  output CLR_2,
  output CLR_3,
  output CLR_4,
  output CLR_5,
  output CLR_6,
  output CLR_7,
  output CLR_8
);

  Multiplexer #(.enable("false"), .select(3), .width(32)) multiplexer_1 (
    .in0(Q), .in1(Q_2), .in2(Q_3), .in3(Q_4), .in4(Q_5), .in5(Q_6), .in6(Q_7), .in7(Q_8), .out(valA),
    .sel(srcA));
  Multiplexer #(.enable("false"), .select(3), .width(32)) multiplexer_2 (
    .in0(Q), .in1(Q_2), .in2(Q_3), .in3(Q_4), .in4(Q_5), .in5(Q_6), .in6(Q_7), .in7(Q_8), .out(valB),
    .sel(srcB));

  assign CLR = reset;
  assign CLR_2 = reset;
  assign CLR_3 = reset;
  assign CLR_4 = reset;
  assign CLR_5 = reset;
  assign CLR_6 = reset;
  assign CLR_7 = reset;
  assign CLR_8 = reset;

  // Notes on the sheet:
  //   Design thinking:
  //   1. Use a multiplexer for each source (srcA and srcB) to
  //   output the register contents for the specified source register.
  //   2. Connect the corresponding inputs for the multiplexer
  //   together in pairs (the two register 0 inputs go the first/top slot).
  //   3. Connect the reset into each of the clear (CLR) outputs for
  //   resetting the registers.
  //   for reg 0
  //   for reg 7
  //   Testing (done in HW3 jointly with regwriter):
  //   Format: valE | dstE | reqE | valM | dstM | reqM | clock | clr | srcA | valA | srcB | valB
  //   00000002 | 000 | 1 | 30000000 | 000 | 1 | 0->1 | 0 | 000 | 00000000 | 000 | 00000000
  //   01031b09 | 010 | 1 | 83001001 | 011 | 1 | 1->0 | 0 | 011 | 00000000 | 010 | 00000000
  //   (values in registers were all 0s before for above test)
  //   01031b09 | 010 | 1 | 83001001 | 011 | 1 | 0->1 | 0 | 011 | 83001001 | 010 | 01031b09
  //   (All tests below are done in succession)
  //   0aa00aa0 | 101 | 0 | f00ff00f | 111 | 1 | 0->1 | 0 | 101 | 00000000 | 111 | f00ff00f
  //   0aa00aa0 | 101 | 0 | f00ff00f | 111 | 1 | 1->0 | 0 | 101 | 00000000 | 111 | f00ff00f 
  //   0aa00aa0 | 101 | 1 | f00ff00f | 111 | 0 | 0->1 | 0 | 101 | 0aa00aa0 | 111 | f00ff00f
  //   0aa00aa0 | 101 | 1 | f00ff00f | 111 | 0 | 0 | 0->1 | 101 | 00000000 | 111 | 00000000
endmodule

module regwriter (
  input  reqE,
  input  [31:0] valE,
  input  [2:0] dstE,
  input  reqM,
  input  [31:0] valM,
  input  [2:0] dstM,
  output [31:0] D0,
  output EN,
  output [31:0] D1,
  output EN_2,
  output [31:0] D2,
  output EN_3,
  output [31:0] D3,
  output EN_4,
  output [31:0] D4,
  output EN_5,
  output [31:0] D5,
  output EN_6,
  output [31:0] D6,
  output EN_7,
  output [31:0] D7,
  output EN_8
);

  wire decoder_1_out0, decoder_1_out1, decoder_1_out2, decoder_1_out3, decoder_1_out4, decoder_1_out5,
       decoder_1_out6, decoder_1_out7, decoder_2_out0, decoder_2_out1, decoder_2_out2, decoder_2_out3,
       decoder_2_out4, decoder_2_out5, decoder_2_out6, decoder_2_out7;
  wire [31:0] demultiplexer_1_out0, demultiplexer_1_out1, demultiplexer_1_out2, demultiplexer_1_out3,
       demultiplexer_1_out4, demultiplexer_1_out5, demultiplexer_1_out6, demultiplexer_1_out7,
       demultiplexer_2_out0, demultiplexer_2_out1, demultiplexer_2_out2, demultiplexer_2_out3,
       demultiplexer_2_out4, demultiplexer_2_out5, demultiplexer_2_out6, demultiplexer_2_out7;

  Demultiplexer #(.enable("false"), .select(3), .width(32)) demultiplexer_1 (
    .out0(demultiplexer_1_out0), .out1(demultiplexer_1_out1), .out2(demultiplexer_1_out2),
    .out3(demultiplexer_1_out3), .out4(demultiplexer_1_out4), .out5(demultiplexer_1_out5),
    .out6(demultiplexer_1_out6), .out7(demultiplexer_1_out7), .in(valE), .sel(dstE));
  Demultiplexer #(.enable("false"), .select(3), .width(32)) demultiplexer_2 (
    .out0(demultiplexer_2_out0), .out1(demultiplexer_2_out1), .out2(demultiplexer_2_out2),
    .out3(demultiplexer_2_out3), .out4(demultiplexer_2_out4), .out5(demultiplexer_2_out5),
    .out6(demultiplexer_2_out6), .out7(demultiplexer_2_out7), .in(valM), .sel(dstM));
  Decoder #(.enable("false"), .select(3)) decoder_1 (
    .out0(decoder_1_out0), .out1(decoder_1_out1), .out2(decoder_1_out2), .out3(decoder_1_out3),
    .out4(decoder_1_out4), .out5(decoder_1_out5), .out6(decoder_1_out6), .out7(decoder_1_out7), .sel(dstE));
  Decoder #(.enable("false"), .select(3)) decoder_2 (
    .out0(decoder_2_out0), .out1(decoder_2_out1), .out2(decoder_2_out2), .out3(decoder_2_out3),
    .out4(decoder_2_out4), .out5(decoder_2_out5), .out6(decoder_2_out6), .out7(decoder_2_out7), .sel(dstM));
  DataENSelect dataenselect_1 (
    .D0(D0), .EN(EN), .valE(demultiplexer_1_out0), .valM(demultiplexer_2_out0), .reqE(reqE),
    .destE(decoder_1_out0), .reqM(reqM), .destM(decoder_2_out0));
  DataENSelect dataenselect_2 (
    .D0(D1), .EN(EN_2), .valE(demultiplexer_1_out1), .valM(demultiplexer_2_out1), .reqE(reqE),
    .destE(decoder_1_out1), .reqM(reqM), .destM(decoder_2_out1));
  DataENSelect dataenselect_3 (
    .D0(D2), .EN(EN_3), .valE(demultiplexer_1_out2), .valM(demultiplexer_2_out2), .reqE(reqE),
    .destE(decoder_1_out2), .reqM(reqM), .destM(decoder_2_out2));
  DataENSelect dataenselect_4 (
    .D0(D3), .EN(EN_4), .valE(demultiplexer_1_out3), .valM(demultiplexer_2_out3), .reqE(reqE),
    .destE(decoder_1_out3), .reqM(reqM), .destM(decoder_2_out3));
  DataENSelect dataenselect_5 (
    .D0(D4), .EN(EN_5), .valE(demultiplexer_1_out4), .valM(demultiplexer_2_out4), .reqE(reqE),
    .destE(decoder_1_out4), .reqM(reqM), .destM(decoder_2_out4));
  DataENSelect dataenselect_6 (
    .D0(D5), .EN(EN_6), .valE(demultiplexer_1_out5), .valM(demultiplexer_2_out5), .reqE(reqE),
    .destE(decoder_1_out5), .reqM(reqM), .destM(decoder_2_out5));
  DataENSelect dataenselect_7 (
    .D0(D6), .EN(EN_7), .valE(demultiplexer_1_out6), .valM(demultiplexer_2_out6), .reqE(reqE),
    .destE(decoder_1_out6), .reqM(reqM), .destM(decoder_2_out6));
  DataENSelect dataenselect_8 (
    .D0(D7), .EN(EN_8), .valE(demultiplexer_1_out7), .valM(demultiplexer_2_out7), .reqE(reqE),
    .destE(decoder_1_out7), .reqM(reqM), .destM(decoder_2_out7));

  // Notes on the sheet:
  //   Design thinking:
  //   1.Use a demultiplexer to send out the data to the correct destination register (as specified by dstE/M). Use a
  //   decoder to determine which register is the destination.
  //   2. Make the EN active only if reqE and dstE or reqM and dstM are active (but not both or neither) 
  //   so we know that something is able to write into the register.
  //   3. Send the data for E or M (as specified by valE/M) to the specified register(s) by using DataENSelect (go to
  //   circuit for more information).
  //   4. If the destinations are the same for both E and M, then the writing is not enabled and the data output will be
  //   all 0s.
  //   Testing (done in HW3 jointly with regreader):
  //   Format: valE | dstE | reqE | valM | dstM | reqM | clock | clr | srcA | valA | srcB | valB
  //   00000002 | 000 | 1 | 30000000 | 000 | 1 | 0->1 | 0 | 000 | 00000000 | 000 | 00000000
  //   01031b09 | 010 | 1 | 83001001 | 011 | 1 | 1->0 | 0 | 011 | 00000000 | 010 | 00000000
  //   (values in registers were all 0s before for above test)
  //   01031b09 | 010 | 1 | 83001001 | 011 | 1 | 0->1 | 0 | 011 | 83001001 | 010 | 01031b09
  //   (All tests below are done in succession)
  //   0aa00aa0 | 101 | 0 | f00ff00f | 111 | 1 | 0->1 | 0 | 101 | 00000000 | 111 | f00ff00f
  //   0aa00aa0 | 101 | 0 | f00ff00f | 111 | 1 | 1->0 | 0 | 101 | 00000000 | 111 | f00ff00f 
  //   0aa00aa0 | 101 | 1 | f00ff00f | 111 | 0 | 0->1 | 0 | 101 | 0aa00aa0 | 111 | f00ff00f
  //   0aa00aa0 | 101 | 1 | f00ff00f | 111 | 0 | 0 | 0->1 | 101 | 00000000 | 111 | 00000000
endmodule

module alu (
  input  [31:0] aluB,
  input  [31:0] aluA,
  input  [3:0] aluOP,
  output [2:0] CC,
  output [31:0] valE
);

  wire addocheck_1_out_4, comparator_1_eq, comparator_1_lt, comparator_2_eq, comparator_2_lt,
       comparator_3_eq, comparator_3_lt, comparator_4_eq, comparator_4_lt, subocheck_1_out_4;
  wire [31:0] adder_1_out, and_1_out, demultiplexer_1_out0, demultiplexer_1_out1, demultiplexer_1_out2,
       demultiplexer_1_out3, demultiplexer_2_out0, demultiplexer_2_out1, demultiplexer_2_out2,
       demultiplexer_2_out3, subtractor_1_out, xor_1_out;

  // Probe on aluB
  // Probe on aluB
  Demultiplexer #(.enable("false"), .select(4), .width(32)) demultiplexer_1 (
    .out0(demultiplexer_1_out0), .out1(demultiplexer_1_out1), .out2(demultiplexer_1_out2),
    .out3(demultiplexer_1_out3), .in(aluB), .sel(aluOP));  // open: out4, out5, out6, out7, out8, out9, out10, out11, out12, out13, out14, out15
  // Probe on aluA
  // Probe on aluA
  Demultiplexer #(.enable("false"), .select(4), .width(32)) demultiplexer_2 (
    .out0(demultiplexer_2_out0), .out1(demultiplexer_2_out1), .out2(demultiplexer_2_out2),
    .out3(demultiplexer_2_out3), .in(aluA), .sel(aluOP));  // open: out4, out5, out6, out7, out8, out9, out10, out11, out12, out13, out14, out15
  Adder #(.width(32)) adder_1 (
    .a(demultiplexer_1_out0), .b(demultiplexer_2_out0), .out(adder_1_out));  // open: cin, cout
  Subtractor #(.width(32)) subtractor_1 (
    .a(demultiplexer_1_out1), .b(demultiplexer_2_out1), .out(subtractor_1_out));  // open: bin, bout
  assign and_1_out = demultiplexer_1_out2 & demultiplexer_2_out2;  // AND_Gate and_1, 32 bits wide
  assign xor_1_out = demultiplexer_1_out3 ^ demultiplexer_2_out3;  // XOR_Gate xor_1, 32 bits wide
  AddOCheck addocheck_1 (
    .out_4(addocheck_1_out_4), .aluB(demultiplexer_1_out0), .aluA(demultiplexer_2_out0), .valE(adder_1_out));
  SubOCheck subocheck_1 (
    .valE(subtractor_1_out), .aluB(demultiplexer_1_out1), .aluA(demultiplexer_2_out1),
    .out_4(subocheck_1_out_4));
  Comparator #(.width(32)) comparator_1 (
    .a(adder_1_out), .b({32{1'b0}}), .eq(comparator_1_eq), .lt(comparator_1_lt));  // open: gt
  Comparator #(.width(32)) comparator_2 (
    .a(subtractor_1_out), .b({32{1'b0}}), .eq(comparator_2_eq), .lt(comparator_2_lt));  // open: gt
  Comparator #(.width(32)) comparator_3 (
    .a(and_1_out), .b({32{1'b0}}), .eq(comparator_3_eq), .lt(comparator_3_lt));  // open: gt
  Comparator #(.width(32)) comparator_4 (
    .a(xor_1_out), .b({32{1'b0}}), .eq(comparator_4_eq), .lt(comparator_4_lt));  // open: gt
  and Z (CC[2], comparator_1_eq, comparator_2_eq, comparator_3_eq, comparator_4_eq);
  or S (CC[1], comparator_1_lt, comparator_2_lt, comparator_3_lt, comparator_4_lt);
  or O (CC[0], addocheck_1_out_4, subocheck_1_out_4, 1'b0, 1'b0);
  assign valE = adder_1_out | subtractor_1_out | and_1_out | xor_1_out;  // OR_Gate or_1, 32 bits wide
  // Probe on valE
  // Probe on valE

  // Notes on the sheet:
  //   0: addl
  //   1: subl
  //   2: andl
  //   3: xorl
  //   Design thinking:
  //   1. Use demultiplexers on each input to get
  //   the correct path for a given operation.
  //   2a. For addl, we send the inputs through an
  //   adder and then send the result to valE,
  //   a comparator (to see if it is 0 or negative), and
  //   to AddOCheck (checks if there is overflow).
  //   2b. For subl, we send the inputs through a
  //   subtractor and then send the result to valE, a
  //   comparator (to see if it is 0 or negative), and to
  //   SubOCheck (checks if there is overflow).
  //   2c. For andl, we send the inputs through an AND
  //   gate and then send the result to valE, a
  //   comparator (to see if it is 0 or negative), and
  //   because the result will never be greater (in
  //   magnitude) than either input, the result will never
  //   overflow.
  //   2d. For xorl, we send the inputs through an XOR
  //   gate and then send the result to valE, a
  //   comparator (to see if it is 0 or negative), and
  //   because the result will never be greater (in
  //   magnitude) than either input, the result will never
  //   overflow.
  //   over max using addl
  //   Z asserted when valE is 0.
  //   S asserted when valE is negative in 2's complement.
  //   O asserted when arithmetic result in valE wrong because
  //   interpreted as signed 2's complement integers.
  //   Testing (done in HW3):
  //   Format: aluB (in hex) | aluA (in hex) | aluOP | Z/S/O | valE (in hex)
  //   00000001 | 00000001 | 0000 |  0/0/0 | 00000002
  //   ffff0001 | 0000ffff | 0000 | 1/0/0 | 00000000
  //   40000000 | 80000000 | 0000 | 0/1/0 | c0000000
  //   00000001 | 7fffffff | 0000 | 0/1/0 | 80000000
  //   10101010 | 0050a000 | 0001 | 0/0/0 | 0fbf7010
  //   80402010 | 80402010 | 0001 | 1/0/0 | 00000000
  //   08888888 | 700c2004 | 0001 | 0/1/0 | 987c6884
  //   7fffffff | 80000000 | 0001 | 0/1/1 | ffffffff
  //   11000011 | 91002210 | 0010 | 0/0/0 | 11000010
  //   88888888 | 44444444 | 0010 | 1/0/0 | 00000000
  //   80000000 | 80000001 | 0010 | 0/1/0 | 80000000
  //   80088008 | 80080000 | 0011 | 0/0/0 | 00008008
  //   01000081 | 01000081 | 0011 | 1/0/0 | 00000000
  //   7fffffff | 80000000 | 0011 | 0/1/0 | ffffffff
  //   [Z,S,O]
endmodule

module MSB (
  input  [31:0] Value,
  output MSB
);


  assign MSB = Value[31];
endmodule

module CND (
  input  [2:0] ZSO,
  input  [3:0] ifun,
  output CND
);

  wire and_1_out, and_2_out, and_3_out, and_4_out, and_5_out, and_6_out, and_7_out, comparator_1_eq,
       comparator_2_eq, comparator_3_eq, comparator_4_eq, comparator_5_eq, comparator_6_eq, comparator_7_eq,
       not_1_out, not_2_out, not_3_out, not_4_out, or_1_out, xor_1_out, xor_2_out, xor_3_out, xor_4_out;

  // Probe on ifun
  Comparator #(.width(4)) comparator_1 (.a(ifun), .b(4'b0000), .eq(comparator_1_eq));  // open: gt, lt
  Comparator #(.width(4)) comparator_2 (.a(ifun), .b(4'b0001), .eq(comparator_2_eq));  // open: gt, lt
  Comparator #(.width(4)) comparator_3 (.a(ifun), .b(4'b0010), .eq(comparator_3_eq));  // open: gt, lt
  Comparator #(.width(4)) comparator_4 (.a(ifun), .b(4'b0011), .eq(comparator_4_eq));  // open: gt, lt
  Comparator #(.width(4)) comparator_5 (.a(ifun), .b(4'b0100), .eq(comparator_5_eq));  // open: gt, lt
  Comparator #(.width(4)) comparator_6 (.a(ifun), .b(4'b0101), .eq(comparator_6_eq));  // open: gt, lt
  Comparator #(.width(4)) comparator_7 (.a(ifun), .b(4'b0110), .eq(comparator_7_eq));  // open: gt, lt
  xor xor_1 (xor_1_out, ZSO[1], ZSO[0]);
  xor xor_2 (xor_2_out, ZSO[1], ZSO[0]);
  xor xor_3 (xor_3_out, ZSO[1], ZSO[0]);
  not not_1 (not_1_out, xor_3_out);
  not not_2 (not_2_out, ZSO[2]);
  or or_1 (or_1_out, xor_1_out, ZSO[2]);
  and and_1 (and_1_out, or_1_out, comparator_2_eq);
  xor xor_4 (xor_4_out, ZSO[1], ZSO[0]);
  and and_2 (and_2_out, xor_4_out, comparator_3_eq);
  and and_3 (and_3_out, ZSO[2], comparator_4_eq);
  not not_3 (not_3_out, ZSO[2]);
  and and_4 (and_4_out, not_3_out, comparator_5_eq);
  not not_4 (not_4_out, xor_2_out);
  and and_5 (and_5_out, not_4_out, comparator_6_eq);
  and and_6 (and_6_out, not_1_out, not_2_out);
  and and_7 (and_7_out, and_6_out, comparator_7_eq);
  or or_2 (CND, comparator_1_eq, and_1_out, and_2_out, and_3_out, and_4_out, and_5_out, and_7_out);

  // Notes on the sheet:
  //   jmp/rrmovl
  //   jle/cmovle
  //   jl/cmovl
  //   je/cmove
  //   jne/cmovne
  //   jge/cmovge
  //   jg/cmovg
  //   Design thinking:
  //   See what flags each condition requires input from.
  //   Determine the circuit logic equivalent to that provided in terms of flags.
  //   Use a comparator for each condition that exists jmp/rrmovl, jle/cmovle,
  //   jl/cmovl, je/cmove, jne/cmovne, jge/cmovge, jg/cmovg.
  //   For each condition, do the necessary logic by using NOT gates for ~,
  //   XOR gates for ^, AND gates for &, and OR gates for |.
  //   At the end, use an OR gate to see if any of the conditions are active.
  //   Testing (done in HW4):
  //   Format: Z (CC) | S (CC) | O (CC) | ifun | condition | output
  //   *NA means that there can be any value
  //   Valid inputs:
  //   NA | NA | NA | 0 | jmp/rrmovl | 1
  //   1/(0) | NA/(1/0) | NA/(0/1) | 1 | jle/cmovle | 1
  //   0 | 1 | 1 | 1 | jle/cmovle | 0
  //   NA | 1/0 | 0/1 | 2 | jl/cmovl | 1
  //   NA | 1 | 1 | 2 | jl/cmovl | 0
  //   1 | NA | NA | 3 | je/cmove | 1
  //   0 | NA | NA | 3 | je/cmove | 0
  //   0 | NA | NA | 4 | jne/cmovne | 1
  //   1 | NA | NA | 4 | jne/cmovne | 0
  //   NA | 1/0 | 1/0 | 5 | jge/cmovge | 1
  //   NA | 1 | 0 | 5 | jge/cmovge | 0
  //   0 | 1/0 | 1/0 | 6 | jg/cmovg | 1
  //   1 | 1 | 1 | 6 | jg/cmovg | 0
endmodule

module ishim (
  input  req,
  input  [31:0] in_2,
  input  reset,
  input  clock,
  input  [7:0] in_5,
  output [7:0] out_6,
  output [7:0] out_7,
  output [7:0] out_8,
  output [7:0] out_9,
  output [7:0] out_10,
  output [7:0] out_11,
  output done,
  output RAMuse,
  output [31:0] out_14,
  output RAMread
);

  wire decoder_1_out0, decoder_1_out1, decoder_1_out2, decoder_1_out3, decoder_1_out4, decoder_1_out5,
       decoder_1_out6, or_1_out;
  wire [2:0] counter_1_q;
  wire [31:0] adder_1_out, bit_extender_1_out;

  D_Flip_Flop #(.enable("true")) d_ff_1 (
    .clk(clock), .D(req), .Q(RAMread), .Qn(done), .preset(1'b0), .en(done), .reset(or_1_out));
  Decoder #(.select(3)) decoder_1 (
    .out0(decoder_1_out0), .out1(decoder_1_out1), .out2(decoder_1_out2), .out3(decoder_1_out3),
    .out4(decoder_1_out4), .out5(decoder_1_out5), .out6(decoder_1_out6), .sel(counter_1_q), .en(RAMread));  // open: out7
  Counter #(.max('h7), .width(3)) counter_1 (
    .load(1'b0), .count(RAMread), .Q(counter_1_q), .up(1'b1), .clk(clock), .clr(or_1_out));  // open: D, carry
  or or_1 (or_1_out, decoder_1_out6, reset);
  assign bit_extender_1_out = {{29{1'b0}}, counter_1_q};  // Bit_Extender bit_extender_1
  Adder #(.width(32)) adder_1 (.a(in_2), .b(bit_extender_1_out), .out(adder_1_out), .cin(1'b0));  // open: cout
  assign out_14 = RAMread ? adder_1_out : 32'bz;  // Controlled_Buffer controlled_buffer_1
  Register #(.trigger("falling")) register_1 (.D(in_5), .en(decoder_1_out0), .Q(out_6), .clk(clock), .clr(reset));
  Register #(.trigger("falling")) register_2 (.D(in_5), .en(decoder_1_out1), .Q(out_7), .clk(clock), .clr(reset));
  Register #(.trigger("falling")) register_3 (.D(in_5), .en(decoder_1_out2), .Q(out_8), .clk(clock), .clr(reset));
  Register #(.trigger("falling")) register_4 (.D(in_5), .en(decoder_1_out3), .Q(out_9), .clk(clock), .clr(reset));
  Register #(.trigger("falling")) register_5 (.D(in_5), .en(decoder_1_out4), .Q(out_10), .clk(clock), .clr(reset));
  Register #(.trigger("falling")) register_6 (.D(in_5), .en(decoder_1_out5), .Q(out_11), .clk(clock), .clr(reset));

  assign RAMuse = RAMread;

  // Notes on the sheet:
  //   addr
  //   in use?
  //   state
  //   (3 bits)
  //   RAMaddr (32 bits)
  //   data from RAM (8 bits)
  //   byte 0
  //   byte 1
  //   byte 2
  //   byte 3
  //   byte 4
  //   byte 5
endmodule

module dhsim (
  input  [31:0] in_1,
  input  [7:0] in_2,
  input  [31:0] in_3,
  input  DMem_Write,
  input  req,
  input  reset,
  input  clock,
  output [31:0] DataOut,
  output [7:0] out_9,
  output RAMwrite,
  output RAMread,
  output done,
  output RAMuse,
  output [31:0] out_14
);

  wire comparator_1_eq, d_ff_1_q, d_ff_1_qn, decoder_1_out0, decoder_1_out1, decoder_1_out2, decoder_1_out3,
       or_1_out;
  wire [1:0] bit_extender_2_out;
  wire [2:0] counter_1_q;
  wire [31:0] adder_1_out, bit_extender_1_out;

  assign bit_extender_1_out = {{29{1'b0}}, counter_1_q};  // Bit_Extender bit_extender_1
  D_Flip_Flop #(.enable("true")) d_ff_1 (
    .clk(clock), .D(DMem_Write), .Q(d_ff_1_q), .Qn(d_ff_1_qn), .preset(1'b0), .en(done), .reset(reset));
  D_Flip_Flop #(.enable("true")) in_use (
    .clk(clock), .D(req), .Q(RAMuse), .Qn(done), .preset(1'b0), .en(done), .reset(or_1_out));
  Adder #(.width(32)) adder_1 (.a(in_1), .b(bit_extender_1_out), .out(adder_1_out), .cin(1'b0));  // open: cout
  and and_1 (RAMwrite, RAMuse, d_ff_1_q);
  and and_2 (RAMread, d_ff_1_qn, RAMuse);
  Decoder #(.select(3)) decoder_1 (
    .out0(decoder_1_out0), .out1(decoder_1_out1), .out2(decoder_1_out2), .out3(decoder_1_out3),
    .sel(counter_1_q), .en(RAMread));  // open: out4, out5, out6, out7
  Counter #(.max('h7), .width(3)) counter_1 (
    .load(1'b0), .count(RAMuse), .Q(counter_1_q), .up(1'b1), .clk(clock), .clr(or_1_out));  // open: D, carry
  or or_1 (or_1_out, comparator_1_eq, reset);
  Comparator #(.mode("unsigned"), .width(3)) comparator_1 (
    .a(counter_1_q), .b(3'b100), .eq(comparator_1_eq));  // open: gt, lt
  assign out_14 = RAMuse ? adder_1_out : 32'bz;  // Controlled_Buffer controlled_buffer_1
  Bit_Extender #(.in_width(3), .out_width(2)) bit_extender_2 (.in(counter_1_q), .out(bit_extender_2_out));
  Multiplexer #(.select(2), .width(8)) multiplexer_1 (
    .in0(in_3[7:0]), .in1(in_3[15:8]), .in2(in_3[23:16]), .in3(in_3[31:24]), .out(out_9),
    .sel(bit_extender_2_out), .en(RAMwrite));
  Register #(.trigger("falling")) register_1 (
    .D(in_2), .en(decoder_1_out0), .Q(DataOut[7:0]), .clk(clock), .clr(reset));
  Register #(.trigger("falling")) register_2 (
    .D(in_2), .en(decoder_1_out1), .Q(DataOut[15:8]), .clk(clock), .clr(reset));
  Register #(.trigger("falling")) register_3 (
    .D(in_2), .en(decoder_1_out2), .Q(DataOut[23:16]), .clk(clock), .clr(reset));
  Register #(.trigger("falling")) register_4 (
    .D(in_2), .en(decoder_1_out3), .Q(DataOut[31:24]), .clk(clock), .clr(reset));

  // Notes on the sheet:
  //   address
  //   writing?
  //   reading?
  //   state
  //   (3 bits)
  //   data in
  //   RAMaddr (32 bits)
  //   data from RAM (8 bits)
  //   data to RAM (8 bits)
endmodule

module kbyte_buddy (
  input  [31:0] addr,
  input  [31:0] addr_prefix,
  input  \use ,
  output [9:0] ram_addr,
  output sel
);

  wire comparator_1_eq;
  wire [31:0] and_1_out;

  Bit_Extender #(.in_width(32), .out_width(10), .\type ("zero")) bit_extender_1 (.in(addr), .out(ram_addr));
  assign and_1_out = addr & 32'hfffffc00;  // AND_Gate and_1, 32 bits wide
  Comparator #(.mode("unsigned"), .width(32)) comparator_1 (
    .a(and_1_out), .b(addr_prefix), .eq(comparator_1_eq));  // open: gt, lt
  and and_2 (sel, comparator_1_eq, \use );
endmodule

module io (
  input  KB_Status,
  input  [6:0] in_2,
  input  RAM_Use,
  input  [31:0] in_4,
  input  [7:0] in_5,
  input  RAM_Read,
  input  RAM_Write,
  input  TTY_Ready,
  input  reset,
  output KB_read_enable,
  output KB_Clear,
  output [7:0] Outgoing_Data,
  output [6:0] out_13,
  output TTY_Enable,
  output TTY_Clear
);

  wire and_1_out, and_2_out, and_3_out, and_4_out, and_5_out, and_6_out, and_7_out, comparator_1_eq,
       comparator_2_eq, comparator_3_eq, comparator_3_gt, comparator_4_eq, comparator_4_gt, comparator_5_eq,
       comparator_5_gt, comparator_6_gt, not_1_out, not_2_out, not_3_out, or_2_out, xor_1_out;
  wire [1:0] multiplexer_1_out, multiplexer_2_out, multiplexer_3_out, multiplexer_4_out, or_1_out;
  wire [7:0] bit_extender_1_out, bit_extender_2_out, bit_extender_3_out, multiplexer_5_out,
       multiplexer_6_out, multiplexer_7_out, multiplexer_8_out, multiplexer_9_out, multiplexer_10_out,
       multiplexer_11_out, multiplexer_12_out, multiplexer_13_out, multiplexer_14_out, undriven;

  // Probe on in_4[7:0]
  Comparator #(.mode("unsigned"), .width(24)) comparator_1 (
    .a(24'hfffe), .b(in_4[31:8]), .eq(comparator_1_eq));  // open: gt, lt
  xor xor_1 (xor_1_out, RAM_Read, RAM_Write);
  Comparator #(.mode("unsigned")) comparator_2 (.a({8{1'b0}}), .b(in_4[7:0]), .eq(comparator_2_eq));  // open: gt, lt
  Comparator #(.mode("unsigned")) comparator_3 (
    .a(8'h4), .b(in_4[7:0]), .gt(comparator_3_gt), .eq(comparator_3_eq));  // open: lt
  Comparator #(.mode("unsigned")) comparator_4 (
    .a(8'h8), .b(in_4[7:0]), .gt(comparator_4_gt), .eq(comparator_4_eq));  // open: lt
  Comparator #(.mode("unsigned")) comparator_5 (
    .a(8'hc), .b(in_4[7:0]), .gt(comparator_5_gt), .eq(comparator_5_eq));  // open: lt
  Comparator #(.mode("unsigned")) comparator_6 (.a(8'h10), .b(in_4[7:0]), .gt(comparator_6_gt));  // open: eq, lt
  and and_1 (and_1_out, RAM_Read, xor_1_out);
  and and_2 (and_2_out, xor_1_out, RAM_Write);
  Multiplexer #(.enable("false"), .width(2)) multiplexer_1 (
    .in0(2'b00), .in1(2'b00), .out(multiplexer_1_out), .sel(comparator_3_gt));
  Multiplexer #(.enable("false"), .width(2)) multiplexer_2 (
    .in0(2'b00), .in1(2'b01), .out(multiplexer_2_out), .sel(and_3_out));
  and and_3 (and_3_out, comparator_4_gt, not_1_out);
  not not_1 (not_1_out, comparator_3_gt);
  and and_4 (and_4_out, comparator_5_gt, not_2_out);
  not not_2 (not_2_out, comparator_4_gt);
  and and_5 (and_5_out, comparator_6_gt, not_3_out);
  not not_3 (not_3_out, comparator_5_gt);
  assign or_1_out = multiplexer_1_out | multiplexer_2_out | multiplexer_3_out | multiplexer_4_out;  // OR_Gate or_1, 2 bits wide
  Multiplexer #(.enable("false"), .width(2)) multiplexer_3 (
    .in0(2'b00), .in1(2'b10), .out(multiplexer_3_out), .sel(and_4_out));
  Multiplexer #(.enable("false"), .width(2)) multiplexer_4 (
    .in0(2'b00), .in1(2'b11), .out(multiplexer_4_out), .sel(and_5_out));
  or or_2 (or_2_out, comparator_3_gt, and_3_out, and_4_out, and_5_out);
  and and_6 (and_6_out, and_2_out, TTY_Ready);
  // Probe on or_1_out
  assign bit_extender_1_out = {{7{1'b0}}, KB_Status};  // Bit_Extender bit_extender_1
  and and_7 (and_7_out, RAM_Use, comparator_1_eq, or_2_out);
  Multiplexer #(.enable("false"), .width(8)) multiplexer_5 (
    .in0({8{1'b0}}), .in1(bit_extender_1_out), .out(multiplexer_5_out), .sel(comparator_2_eq));
  Multiplexer #(.enable("false"), .width(8)) multiplexer_6 (
    .in0({8{1'b0}}), .in1(bit_extender_3_out), .out(multiplexer_6_out), .sel(comparator_3_eq));
  Multiplexer #(.enable("false"), .width(8)) multiplexer_7 (
    .in0({8{1'b0}}), .in1(in_5), .out(multiplexer_7_out), .sel(comparator_5_eq));
  Multiplexer #(.enable("false"), .width(8)) multiplexer_8 (
    .in0({8{1'b0}}), .in1(bit_extender_2_out), .out(multiplexer_8_out), .sel(comparator_4_eq));
  assign bit_extender_2_out = {{7{1'b0}}, TTY_Ready};  // Bit_Extender bit_extender_2
  assign bit_extender_3_out = {{1{1'b0}}, in_2};  // Bit_Extender bit_extender_3
  Multiplexer #(.enable("false"), .select(2), .width(8)) multiplexer_9 (
    .in0(multiplexer_5_out), .in1(multiplexer_6_out), .in2(multiplexer_8_out), .in3(multiplexer_7_out),
    .out(multiplexer_9_out), .sel(or_1_out));
  Multiplexer #(.enable("false"), .width(8)) multiplexer_10 (
    .in1(multiplexer_9_out), .out(multiplexer_10_out), .sel(and_1_out));  // open: in0
  Multiplexer #(.enable("false"), .width(8)) multiplexer_11 (
    .in1(multiplexer_9_out), .out(multiplexer_11_out), .sel(and_1_out));  // open: in0
  Multiplexer #(.enable("false"), .width(8)) multiplexer_12 (
    .in1(multiplexer_9_out), .out(multiplexer_12_out), .sel(and_1_out));  // open: in0
  Multiplexer #(.enable("false"), .width(8)) multiplexer_13 (
    .in1(multiplexer_9_out), .out(multiplexer_13_out), .sel(and_6_out));  // open: in0
  // Probe on multiplexer_10_out
  // Probe on multiplexer_11_out
  // Probe on multiplexer_12_out
  // Probe on multiplexer_13_out
  and and_8 (KB_read_enable, and_3_out, and_1_out, and_7_out);
  Bit_Extender #(.out_width(7), .\type ("zero")) bit_extender_4 (.in(multiplexer_13_out), .out(out_13));
  and and_9 (TTY_Enable, and_5_out, and_7_out, and_6_out);
  // Probe on out_13
  Multiplexer #(.enable("false"), .select(2), .width(8)) multiplexer_14 (
    .in0(multiplexer_10_out), .in1(multiplexer_11_out), .in2(multiplexer_12_out), .out(multiplexer_14_out),
    .sel(or_1_out));  // open: in3
  Multiplexer #(.enable("false"), .width(8)) multiplexer_15 (
    .in0(undriven), .in1(multiplexer_14_out), .out(Outgoing_Data), .sel(and_7_out));

  assign KB_Clear = reset;
  assign TTY_Clear = reset;

  // Notes on the sheet:
  //   Design thinking:
  //   1. Check if RAM use is enabled and if the RAM address is valid.
  //   If so, let the data be outputted to outgoing data. If not, output
  //   floating to the outgoing data.
  //   2. Use multiplexers to create a 2-bit selector to use with other
  //   multiplexers.
  //   3. Make sure that RAM Read and RAM Write are not on at the
  //   same time.
  //   4. Use multiplexers that take whether or not the least significant
  //   byte is being referred to for KBSR, KBDR, DSR, or DDR. If so,
  //   send through the respective data input. If not, send through 00
  //   through.
  //   5. Use multiplexers connected to RAM Read (KBSR, KBDR, DSR)
  //   or RAM Write (DDR) to determine which, if any, of KBSR, KBDR,
  //   DSR, or DDR are being referred to. For any of them, if they are
  //   active, then send the input data through. If not, send through a
  //   floating value.
  //   6. Use a multiplexer and select the correct data input by using
  //   the 2-bit selector value (made earlier) to get the right data.
  //   7. Use a mulitplexer to send through floating if the condition from
  //   step 1 is off or the data input if the condition from step 1 is on.
  //   RAM Address
  //   Incoming Data
  //   KBSR
  //   KBDR
  //   DSR
  //   DDR
  //   KB Data
  //   TTY Data
  //   Testing (done in HW5 in larger test circuit provided): 
  //   KBSR (All register 0)
  //   (KB Status | RAMuse | RAMaddr | RAMread | RAMwrite | data out):
  //   1 | 1 | 00fffe00 | 1 | 0 | 01,
  //   1 | 0 | 00fffe00 | 1 | 0 | xx,
  //   1 | 1 | 00fffe01 | 1 | 0 | 00,
  //   1 | 1 | 00fffe00 | 1 | 1 | xx
  //   KBDR (All register 1)
  //   (KB Data | RAMuse | RAMaddr | RAMread | RAMwrite | KB RdEn | data out):
  //   h | 1 | 00fffe04 | 1 | 0 | 1 | 68,
  //   h | 0 | 00fffe04 | 1 | 0 | 0 | xx,
  //   h | 1 | 00fffe05 | 1 | 0 | 1 | 00,
  //   h | 1 | 00fffe04 | 1 | 1 | 0 | xx
  //   DSR (All register 2)
  //   (TTY Ready | RAMuse | RAMaddr | RAMread | RAMwrite | data out):
  //   1 | 1 | 00fffe08 | 1 | 0 | 01,
  //   0 | 1 | 00fffe08 | 1 | 0 | 00,
  //   1 | 1 | 00fffe08 | 0 | 1 | xx,
  //   1 | 1 | 00fffe09 | 1 | 0 | 00
  //   DDR (All register 3) *TTY Data after clock press
  //   (data in | RAMuse | RAMaddr | RAMread | RAMwrite | TTY Ready | TTY Enable | TTY Data):
  //   41 | 1 | 00fffe0c | 0 | 1 | 1 | 1 | A,
  //   41 | 0 | 00fffe0c | 0 | 1 | 1 | 0 | (nothing),
  //   41 | 1 | 00fffe0c | 0 | 1 | 0 | 0 | (nothing),
  //   41 | 1 | 00fffe0d | 0 | 1 | 1 | 1 | (nothing),
  //   41 | 1 | 00fffe0c | 1 | 0 | 1 | 0 | (nothing)
endmodule

module FSM (
  input  clock,
  input  reset,
  input  [3:0] icode,
  input  DMemDone,
  input  IMemDone,
  output [23:0] \output ,
  output [5:0] state
);

  // Probe on nothing
endmodule

module DataENSelect (
  input  [31:0] valE,
  input  [31:0] valM,
  input  reqE,
  input  destE,
  input  reqM,
  input  destM,
  output [31:0] D0,
  output EN
);

  wire and_2_out, and_3_out, not_1_out;
  wire [0:0] and_1_out;

  // Probe on {EN, and_1_out[0]}
  Multiplexer #(.enable("false"), .select(2), .width(32)) multiplexer_1 (
    .in0({32{1'b0}}), .in1({32{1'b0}}), .in2(valE), .in3(valM), .out(D0), .sel({EN, and_1_out[0]}));
  and and_1 (and_1_out[0], not_1_out, and_3_out);
  not not_1 (not_1_out, and_2_out);
  and and_2 (and_2_out, reqE, destE);
  and and_3 (and_3_out, reqM, destM);
  xor xor_1 (EN, and_2_out, and_3_out);

  // Notes on the sheet:
  //   Design thinking:
  //   1. Send the data for E or M (as specified by valE/M) to the specified register(s) by using a multiplexer. We select
  //   the correct input by checking if the destination and reqE/M is active for each input. (The inverter ensures that the
  //   second input is selected only if the second input and destination are active when we check with the AND gate)
  //   2. If the destinations are the same for both E and M, then the writing is not enabled. (The 2 AND gates and the
  //   following XOR gate that lead into EN ensure that if the value for E or M refers to the same register, then the 
  //   data for both E and M are not sent through by making EN inactive, which selects and sends the 32-bit data that 
  //   contains all 0s to the data output instead)
endmodule

module SubOCheck (
  input  [31:0] valE,
  input  [31:0] aluB,
  input  [31:0] aluA,
  output out_4
);

  wire and_1_out, and_2_out, comparator_1_gt, comparator_1_lt, comparator_2_gt, comparator_3_lt,
       comparator_4_lt, comparator_5_gt;

  Comparator #(.width(32)) comparator_1 (
    .a(valE), .b({32{1'b0}}), .gt(comparator_1_gt), .lt(comparator_1_lt));  // open: eq
  Comparator #(.width(32)) comparator_2 (.a(aluB), .b({32{1'b0}}), .gt(comparator_2_gt));  // open: eq, lt
  Comparator #(.width(32)) comparator_3 (.a(aluB), .b({32{1'b0}}), .lt(comparator_3_lt));  // open: gt, eq
  Comparator #(.width(32)) comparator_4 (.a(aluA), .b({32{1'b0}}), .lt(comparator_4_lt));  // open: gt, eq
  Comparator #(.width(32)) comparator_5 (.a(aluA), .b({32{1'b0}}), .gt(comparator_5_gt));  // open: eq, lt
  and and_1 (and_1_out, comparator_2_gt, comparator_1_lt, comparator_4_lt);
  and and_2 (and_2_out, comparator_3_lt, comparator_1_gt, comparator_5_gt);
  or or_1 (out_4, and_1_out, and_2_out);

  // Notes on the sheet:
  //   Design thinking:
  //   Checks if subtraction of two inputs results in overflow.
  //   Assume B-A format in this explanation.
  //   1. Check if input B is positive and input A is negative but
  //   produces a negative number or if input B is negative and
  //   input A is positive and produces a positive number.
  //   2. If either is true, then there is overflow.
endmodule

module AddOCheck (
  input  [31:0] valE,
  input  [31:0] aluB,
  input  [31:0] aluA,
  output out_4
);

  wire and_1_out, and_2_out, comparator_1_gt, comparator_1_lt, comparator_2_gt, comparator_3_lt,
       comparator_4_gt, comparator_5_lt;

  Comparator #(.width(32)) comparator_1 (
    .a(valE), .b({32{1'b0}}), .gt(comparator_1_gt), .lt(comparator_1_lt));  // open: eq
  Comparator #(.width(32)) comparator_2 (.a(aluB), .b({32{1'b0}}), .gt(comparator_2_gt));  // open: eq, lt
  Comparator #(.width(32)) comparator_3 (.a(aluB), .b({32{1'b0}}), .lt(comparator_3_lt));  // open: gt, eq
  Comparator #(.width(32)) comparator_4 (.a(aluA), .b({32{1'b0}}), .gt(comparator_4_gt));  // open: eq, lt
  Comparator #(.width(32)) comparator_5 (.a(aluA), .b({32{1'b0}}), .lt(comparator_5_lt));  // open: gt, eq
  and and_1 (and_1_out, comparator_2_gt, comparator_1_lt, comparator_4_gt);
  and and_2 (and_2_out, comparator_3_lt, comparator_1_gt, comparator_5_lt);
  or or_1 (out_4, and_1_out, and_2_out);

  // Notes on the sheet:
  //   Design thinking:
  //   Checks if addition of 2 inputs results in overflow.
  //   1. Check if both inputs are positive but produce a negative
  //   result or if both inputs are negative but produce a positive
  //   result.
  //   2. If either is true, then there is overflow.
endmodule

module Microsequencer (
  input  [5:0] CurrentState,
  input  [1:0] select,
  input  [3:0] icode,
  input  [5:0] valN,
  input  DMemReady,
  input  IMemReady,
  input  exception,
  input  privCODEfail,
  output [5:0] NextState
);

  wire [5:0] bit_extender_1_out, demultiplexer_1_out0, demultiplexer_1_out1, demultiplexer_1_out2,
       demultiplexer_1_out3, multiplexer_1_out, multiplexer_2_out, multiplexer_3_out, multiplexer_4_out;

  assign bit_extender_1_out = {{2{1'b1}}, icode};  // Bit_Extender bit_extender_1
  // Probe on demultiplexer_1_out0
  Demultiplexer #(.enable("false"), .select(2), .width(6)) demultiplexer_1 (
    .out0(demultiplexer_1_out0), .out1(demultiplexer_1_out1), .out2(demultiplexer_1_out2),
    .out3(demultiplexer_1_out3), .in(CurrentState), .sel(select));
  // Probe on bit_extender_1_out
  // Probe on demultiplexer_1_out1
  // Probe on demultiplexer_1_out2
  // Probe on demultiplexer_1_out3
  Multiplexer #(.enable("false"), .width(6)) multiplexer_1 (
    .in0(demultiplexer_1_out3), .in1(bit_extender_1_out), .out(multiplexer_1_out), .sel(IMemReady));
  Multiplexer #(.enable("false"), .width(6)) multiplexer_2 (
    .in0(demultiplexer_1_out2), .in1(valN), .out(multiplexer_2_out), .sel(DMemReady));
  Multiplexer #(.enable("false"), .select(2), .width(6)) multiplexer_3 (
    .in0(demultiplexer_1_out0), .in1(valN), .in2(multiplexer_2_out), .in3(multiplexer_1_out),
    .out(multiplexer_3_out), .sel(select));
  Multiplexer #(.enable("false"), .width(6)) multiplexer_4 (
    .in0(multiplexer_3_out), .in1(6'b111110), .out(multiplexer_4_out), .sel(exception));
  Multiplexer #(.enable("false"), .width(6)) multiplexer_5 (
    .in0(multiplexer_4_out), .in1(6'b110000), .out(NextState), .sel(privCODEfail));

  // Notes on the sheet:
  //   Testing (done in HW5) (CurrentState | select | icode | valN | DMemReady | IMemReady | NextState):
  //   101010 | 00 | 0000 | 000000 | 0 | 0 | 101010,
  //   101010 | 00 | 1111 | 111111 | 1 | 1 | 101010,
  //   000000 | 01 | 0000 | 010101 | 0 | 0 | 010101,
  //   111111 | 01 | 1111 | 010101 | 1 | 1 | 010101,
  //   101010 | 10 | 0000 | 010101 | 0 | 0 | 101010,
  //   101010 | 10 | 0000 | 010101 | 1 | 0 | 010101,
  //   101010 | 10 | 1111 | 010101 | 0 | 1 | 101010,
  //   101010 | 11 | 0101 | 000000 | 0 | 0 | 101010,
  //   101010 | 11 | 0101 | 000000 | 0 | 1 | 110101,
  //   101010 | 11 | 0101 | 111111 | 0 | 1 | 110101
  //   Design thinking:
  //   Use a demultiplexer to handle the four cases for select (00,
  //   01, 10, 11).
  //   1. Take the select bits and send them into the demultiplexer 
  //   to select the correct next state.
  //   2a. If select is 00, then take the current state and directly send
  //   it to the multiplexer to be outputted to next state.
  //   2b. If select is 01, then send valN directly to the multiplexer to be outputted
  //   to the next state.
  //   2c. If select is 10, then send current state (if DMemReady is 0) or valN
  //   (if DMemReady is 1) directly to the multiplexer to be outputted to the next
  //   state.
  //   2d. If select is 11, then send the current state (if IMemReady is 0) or
  //   the icode with 2 bits containing 1 in front (if IMemReady is 1) directly
  //   to the multiplexer to be outputted to the next state.
  //   3. The multiplexer at the end outputs whichever next state is selected by
  //   the 2-bit select.
  //   If exception is thrown because of an invalid instruction that trying to be
  //   run in user mode, then a multiplexer is used to
  //   send the exception handling state as the next state.
  //   If the instruction is invalid and was trying to be run in privileged mode, 
  //   then a multiplexer is used to send the halt state as the next state.
endmodule
